# Fritzing sketch microduino-arduino-isp (saved by Fritzing 0.9.2b)
circuit board: 8.46667cm x 5.64444cm

parts:
  Microduino_ISP = Microduino-Core+
  Microduino = Microduino-Core+

nets:
  GND: Microduino_ISP.GND, Microduino.GND
  N1: Microduino_ISP.D13, Microduino.D13
  N2: Microduino_ISP.D12, Microduino.D12
  N3: Microduino_ISP.D11, Microduino.D11
  N4: Microduino_ISP.D10, Microduino.RST
  3V3: Microduino_ISP.3V3, Microduino.3V3
  5V: Microduino_ISP.5V, Microduino.5V

custom parts:
  Microduino-Core+: The awesome Arduino compatible microcontroller
